# Fritzing sketch door-sensor (saved by Fritzing 0.9.3b)
circuit board: 6.99262cm x 4.57678cm
breadboards: 1

parts:
  R1 = Resistor [tolerance=±5% resistance=47k package=THT]
  R2 = Resistor [tolerance=±5% resistance=10k package=THT]
  LED1 = LED - 5mm [color="Green (570nm)" package="5 mm [THT]"]
  R3 = Resistor [tolerance=±5% resistance=220 package=THT]
  S1 = Magnetic Door Switch [package=reed_switch_plastic]
  Pad1 = Pad [width=1.6929965866644083 height=1.6594118875221233 connect=center]
  Pad2 = Pad [width=1.6929965866644083 height=1.6594118875221233 connect=center]
  Part1 = Adafruit Feather HUZZAH ESP8266 [part_number="Adafruit #2821"]

nets:
  N1: R1.Pin_0, Part1.VBAT
  N2: R1.Pin_1, R2.Pin_1, Part1.ADC
  N3: R2.Pin_0, LED1.cathode, S1.Magnetic_door_switch, Part1.GND
  N4: LED1.anode, R3.Pin_0
  N5: R3.Pin_1, Part1.GPIO2
  N6: S1.2, Part1.GPIO12/MISO
  N7: Pad1.pad, Pad2.pad, Part1.RESET, Part1.GPIO16

notes:
  Window/Door sensor by kenken64

custom parts:
  Adafruit Feather HUZZAH ESP8266: his is the Adafruit Feather HUZZAH ESP8266 - our take on an 'all-in-one' ESP8266 WiFi development board with built in USB and battery charging. Its an ESP8266 WiFi module with all the extras you need, ready to rock! We have other boards in the Feather family, check'em out here. At the Feather HUZZAH's heart is an ESP8266 WiFi microcontroller clocked at 80 MHz and at 3.3V logic. This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
